// Logisim project alu.circ as structural Verilog: 1 circuit, main circuit ALU
module ALU (
  input  [31:0] A,
  input  [31:0] B,
  input  [3:0] ALU_Op,
  output [31:0] Out,
  output Equal,
  output LT,
  output LTU
);

  wire carry;
  wire [31:0] add, sll, srl;

  Multiplexer #(.select(4), .width(32)) multiplexer_1 (
    .in0(sll), .in1(srl), .in2(add), .out(Out), .sel(ALU_Op));  // open: in3, in4, in5, in6, in7, in8, in9, in10, in11, in12, in13, in14, in15, en
  Shifter #(.width(32)) shifter_1 (.in(A), .\dist (B[4:0]), .out(sll));
  Shifter #(.width(32), .shift("lr")) shifter_2 (.in(A), .\dist (B[4:0]), .out(srl));
  Adder #(.width(32)) adder_1 (.a(A), .b(B), .out(add), .cout(carry));  // open: cin

  // Other names for the same wires on the sheet: Op[3:0] = ALU_Op

  // Notes on the sheet:
  //   Inputs
  //   NOTE
  //   Please do not modify/replace/move/change/delete/etc input and output pins
  //   Outputs
endmodule
